// Logisim project alu.circ as structural Verilog: 1 circuit, main circuit main
module main (
  input  [15:0] X,
  input  [15:0] Y,
  input  [2:0] Switch,
  output Signed_Overflow,
  output Equal,
  output [15:0] Result,
  output [15:0] Result_2
);


  // Other names for the same wires on the sheet: overflow = Signed_Overflow; S[2:0] = Switch

  // Notes on the sheet:
  //   INPUTS to your circuit
  //   DON'T CHANGE THE LOCATIONS OF THE INPUTS AND OUTPUTS!
  //   OUTPUTS from your circuit
endmodule
